# Fritzing sketch door-opener (saved by Fritzing 0.9.10b)
breadboards: 2

parts:
  U1 = ESP32-38PinWide [part_number=ESP32-38PinWide]
  S4 = Pushbutton [package="[THT]"]
  J1 = Basic Servo
  R1 = Resistor [tolerance=±5% resistance=220 package="0603 [SMD]"]
  LED1 = LEDs [package=led10mm]

nets:
  N1: U1.GPIO36, S4.Pin_3, S4.Pin_4, R1.Pin_1
  N2: U1.GPIO12, LED1.A
  N3: U1.GND, LED1.C
  N4: U1.GPIO18, J1.pulse
  N5: S4.Pin_1, S4.Pin_2, J1.vcc
  N6: J1.gnd, R1.Pin_0

custom parts:
  ESP32-38PinWide: Generic 38-Pin ESP32 with wide format (only access to one side of pins on a breadboard) based on Stephen Lilley's HiLetgo ESP-WROOM-32 ESP32 ESP-32S Development Board.
